# Fritzing sketch PowerMonitor (saved by Fritzing 0.9.2b)
breadboards: 3

parts:
  ESP-12-Breakout1 = ESP-12-Breakout [part_number=ESP8266]
  RXTX = female pin header, 4 pins [form="♀ (female)"]
  J2_5V = female pin header, 2 pins [form="♀ (female)"]
  J3_3_3V = female pin header, 3 pins [form="♀ (female)"]
  C1 = Electrolytic Capacitor [capacitance=10µF package="100 mil [THT, electrolytic]"]
  Part1 = Bi-Directional Logic Level Converter [part_number=BOB-12009]

nets:
  N1: ESP-12-Breakout1.CH_PD, ESP-12-Breakout1.VCC, J3_3_3V.pin2, C1.-, Part1.LV
  N2: ESP-12-Breakout1.TXD, Part1.LV1
  N3: ESP-12-Breakout1.RXD, Part1.LV2
  GND: ESP-12-Breakout1.GPIO15, ESP-12-Breakout1.GND, RXTX.pin1, J2_5V.pin2, J3_3_3V.pin3, C1.+, Part1.GND
  N4: RXTX.pin2, J2_5V.pin1, J3_3_3V.pin1, Part1.HV
  N5: RXTX.pin3, Part1.HV1
  N6: RXTX.pin4, Part1.HV2

custom parts:
  Bi-Directional Logic Level Converter: Description: If you've ever tried to connect a 3.3V device to a 5V system, you know what a challenge it can be. The SparkFun bi-directional logic level converter is a small device that safely steps down 5V signals to 3.3V AND steps up 3.3V to 5V at the same time. This level converter also works with 2.8V and 1.8V devices. What really separates this Logic level converter from our previous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
