# Fritzing sketch SmartSocket (saved by Fritzing 0.9.2b)
breadboards: 1

parts:
  part = NPN-Transistor [part_number=BC182 package="TO92 [THT]"]
  part_2 = PNP-Transistor [part_number=BC212 package="TO92 [THT]"]
  part_3 = TRIAC [part_number=BT138 package=to-92]
  part_4 = Resistor [tolerance=±5% resistance=10k package=THT]
  part_5 = Resistor [tolerance=±5% resistance=100k package=THT]
  part_6 = Resistor [tolerance=±5% resistance=220 package=THT]
  J2_220V = Screw terminal - 2 pins [package=THT]
  Power_plug1_5V = Power plug
  J1_3V = female pin header, 2 pins [form="♀ (female)"]

nets:
  N1: part.E, part_3.M1, J2_220V.pin1, Power_plug1_5V.GND, J1_3V.pin1
  N2: part.B, part_5.Pin_1
  N3: part.C, part_2.B, part_4.Pin_0
  N4: part_2.E, part_4.Pin_1, Power_plug1_5V.VCC
  N5: part_2.C, part_6.Pin_0
  N6: part_3.G, part_6.Pin_1
  N7: part_3.M2, J2_220V.pin2
  N8: part_5.Pin_0, J1_3V.pin2
